# Fritzing sketch sketch (saved by Fritzing 0.9.3b)

parts:
  Part1 = node32s
  Part2 = MicroSD Card Module
  Part3 = Breakout Board for Electret Microphone

nets:
  N1: Part1.IO34, Part3.AUD
  VCC: Part1.5V, Part2.VCC, Part3.VCC
  GND: Part1.GND, Part2.GND, Part3.GND
  N2: Part1.IO23, Part2.MOSI
  N3: Part1.IO19, Part2.MISO
  N4: Part1.IO18, Part2.SCK
  N5: Part1.IO5, Part2.CS
